// Logisim project 2bit-adder.circ as structural Verilog: 1 circuit, main circuit main
module main (
  input  A1,
  input  A0,
  input  B1,
  input  B0
);

  wire and_1_out, and_2_out, and_3_out, or_1_out, xor_1_out, xor_2_out, xor_3_out;

  or or_1 (or_1_out, and_1_out, and_2_out);
  and and_1 (and_1_out, B1, A1);
  LED led_1 (.in(xor_3_out));
  LED led_2 (.in(or_1_out));
  LED led_3 (.in(xor_2_out));
  and and_2 (and_2_out, and_3_out, xor_1_out);
  xor xor_1 (xor_1_out, A1, B1);
  xor xor_2 (xor_2_out, xor_1_out, and_3_out);
  and and_3 (and_3_out, A0, B0);
  xor xor_3 (xor_3_out, A0, B0);

  // Notes on the sheet:
  //   2^1
  //   2-Bit Adder
  //   2^1
  //   2^2
  //   2^0
  //   S1
  //   S2
  //   S0
  //   2^0
  //   2^0
  //   2^1
  //   http://www.spec.gmu.edu/~pparis/classes/notes_101/node112.html
endmodule
