// Logisim project 4bit-adder.circ as structural Verilog: 1 circuit, main circuit main
module main (
  input  a0,
  input  a1,
  input  a2,
  input  a3,
  input  b0,
  input  b1,
  input  b2,
  input  b3
);

  wire and_1_out, and_2_out, and_3_out, and_4_out, and_5_out, and_6_out, and_7_out, xor_1_out, xor_2_out,
       xor_3_out, xor_4_out, xor_5_out, xor_6_out, xor_7_out, xor_8_out, xor_9_out, xor_10_out;

  xor xor_1 (xor_1_out, a0, b0);
  and and_1 (and_1_out, b0, a0);
  xor xor_2 (xor_2_out, a1, b1);
  and and_2 (and_2_out, b1, a1);
  xor xor_3 (xor_3_out, a2, b2);
  and and_3 (and_3_out, b2, a2);
  xor xor_4 (xor_4_out, a3, b3);
  and and_4 (and_4_out, b3, a3);
  xor xor_5 (xor_5_out, xor_2_out, and_1_out);
  and and_5 (and_5_out, and_1_out, xor_2_out);
  xor xor_6 (xor_6_out, xor_3_out, xor_8_out);
  and and_6 (and_6_out, xor_8_out, xor_3_out);
  xor xor_7 (xor_7_out, xor_4_out, xor_9_out);
  and and_7 (and_7_out, xor_9_out, xor_4_out);
  xor xor_8 (xor_8_out, and_5_out, and_2_out);
  xor xor_9 (xor_9_out, and_6_out, and_3_out);
  xor xor_10 (xor_10_out, and_7_out, and_4_out);
  LED led_1 (.in(xor_1_out));
  LED led_2 (.in(xor_5_out));
  LED led_3 (.in(xor_6_out));
  LED led_4 (.in(xor_7_out));
  LED led_5 (.in(xor_10_out));

  // Notes on the sheet:
  //   s0
  //   s1
  //   s2
  //   s3
  //   s4 / Carry
endmodule
