// Logisim project full-adder.circ as structural Verilog: 1 circuit, main circuit main
module main (
  input  A,
  input  B,
  input  C
);

  wire and_1_out, and_2_out, or_1_out, xor_1_out, xor_2_out;

  xor xor_1 (xor_1_out, A, B);
  and and_1 (and_1_out, C, xor_1_out);
  and and_2 (and_2_out, A, B);
  LED led_1 (.in(or_1_out));
  xor xor_2 (xor_2_out, xor_1_out, C);
  or or_1 (or_1_out, and_1_out, and_2_out);
  LED led_2 (.in(xor_2_out));

  // Notes on the sheet:
  //   Full-Adder
  //   https://www.geeksforgeeks.org/full-adder-in-digital-logic/
  //   2^1
  //   2^0
endmodule
