// Logisim project half-adder.circ as structural Verilog: 1 circuit, main circuit main
module main (
  input  A,
  input  B
);

  wire and_1_out, xor_1_out;

  xor xor_1 (xor_1_out, A, B);
  and and_1 (and_1_out, A, B);
  LED led_1 (.in(xor_1_out));
  LED led_2 (.in(and_1_out));

  // Notes on the sheet:
  //   Half-Adder
  //   2^1
  //   https://www.geeksforgeeks.org/half-adder-in-digital-logic/#
  //   2^0
endmodule
